# Fritzing sketch allSwitchesCircuit (saved by Fritzing 0.9.2b)
breadboards: 1

parts:
  S1 = Momentary Switch [package=tactile_switch_smd]
  S2 = Momentary Switch [package=tactile_switch_smd]
  S3 = Momentary Switch [package=tactile_switch_smd]
  S4 = Momentary Switch [package=tactile_switch_smd]
  S5 = Momentary Switch [package=tactile_switch_smd]
  S6 = Momentary Switch [package=tactile_switch_smd]
  S7 = Momentary Switch [package=tactile_switch_smd]
  S8 = Momentary Switch [package=tactile_switch_smd]
  S9 = Momentary Switch [package=tactile_switch_smd]
  S10 = Momentary Switch [package=tactile_switch_smd]
  S11 = Momentary Switch [package=tactile_switch_smd]
  S12 = Momentary Switch [package=tactile_switch_smd]
  R1 = Resistor [tolerance=±5% resistance=220 package=THT]
  R2 = Resistor [tolerance=±5% resistance=220 package=THT]
  R3 = Resistor [tolerance=±5% resistance=220 package=THT]
  J1 = female pin header, 3 pins [form="♀ (female)"]
  J2 = female pin header, 2 pins [form="♀ (female)"]
  J3 = female pin header, 2 pins [form="♀ (female)"]

nets:
  N1: S1.2, S2.2, S3.2, J2.pin1
  N2: S1.4, S4.4, S7.4, S11.4, R3.Pin_1
  N3: S2.4, S5.4, S8.4, S10.4, R2.Pin_1
  N4: S3.4, S6.4, S9.4, S12.4, R1.Pin_1
  N5: S4.1, J2.pin2
  N6: S4.2, S5.2, S6.2
  N7: S7.1, J3.pin1
  N8: S7.2, S8.2, S9.2
  N9: S10.2, S11.2, S12.2
  N10: S10.3, J1.pin2
  N11: S11.1, J3.pin2
  N12: S11.3, J1.pin1
  N13: S12.3, J1.pin3
  GND: R1.Pin_0, R2.Pin_0, R3.Pin_0
