# Fritzing sketch debugSwitchesCircuit (saved by Fritzing 0.9.2b)
breadboards: 1

parts:
  S1 = Momentary Switch [package=tactile_switch_smd]
  S2 = Momentary Switch [package=tactile_switch_smd]
  S3 = Momentary Switch [package=tactile_switch_smd]
  S4 = Momentary Switch [package=tactile_switch_smd]
  S5 = Momentary Switch [package=tactile_switch_smd]
  S6 = Momentary Switch [package=tactile_switch_smd]
  S7 = Momentary Switch [package=tactile_switch_smd]
  S8 = Momentary Switch [package=tactile_switch_smd]
  S9 = Momentary Switch [package=tactile_switch_smd]
  S10 = Momentary Switch [package=tactile_switch_smd]
  S11 = Momentary Switch [package=tactile_switch_smd]
  S12 = Momentary Switch [package=tactile_switch_smd]
  J1 = female pin header, 12 pins [form="♀ (female)"]
  J2 = female pin header, 6 pins [form="♀ (female)"]
  J3 = female pin header, 6 pins [form="♀ (female)"]

nets:
  N1: S1.2, J1.pin12
  N2: S1.4, J2.pin6
  N3: S2.2, J1.pin10
  N4: S2.4, J2.pin1
  N5: S3.2, J1.pin8
  N6: S3.4, J2.pin2
  N7: S4.2, J1.pin11
  N8: S4.4, J2.pin5
  N9: S5.2, J1.pin9
  N10: S5.4, J2.pin4
  N11: S6.2, J1.pin7
  N12: S6.4, J2.pin3
  N13: S7.2, J1.pin6
  N14: S7.4, J3.pin6
  N15: S8.2, J1.pin4
  N16: S8.4, J3.pin1
  N17: S9.2, J1.pin2
  N18: S9.4, J3.pin2
  N19: S10.2, J1.pin3
  N20: S10.4, J3.pin4
  N21: S11.2, J1.pin5
  N22: S11.4, J3.pin5
  N23: S12.2, J1.pin1
  N24: S12.4, J3.pin3
