# Fritzing sketch switchCircuit_1 (saved by Fritzing 0.9.2b)
breadboards: 1

parts:
  S1 = Momentary Switch [package=tactile_switch_smd]
  R1 = Resistor [tolerance=±5% resistance=1k package=THT]
  V1 = DC Power [voltage=5]
  J1 = female pin header, 2 pins [form="♀ (female)"]

nets:
  N1: S1.1, V1.V+
  N2: S1.3, R1.Pin_0
  GND: R1.Pin_1, V1.V-, J1.pin2

notes:
  MCU Input
  MX Switch
